// Logisim project projeto_graphics_cards.circ as structural Verilog: 3 circuits, main circuit Graphics_Card_256x128
module Graphics_Card_256x128 (
  input  R
);

  wire adder_1_cout, clock_1_out;
  wire [6:0] adder_2_out, bit_extender_2_out, rgb_video_1_p5;
  wire [7:0] adder_1_out, bit_extender_1_out, rgb_video_1_p4;
  wire [23:0] rgb_video_1_p6;

  Clock clock_1 (.out(clock_1_out));
  // RGB_Video #(.cursor("No Cursor"), .width(256)) rgb_video_1: pin names not known; wires that end beside it: R, clock_1_out, clock_1_out, rgb_video_1_p4, rgb_video_1_p5, rgb_video_1_p6
  Register register_1 (.D(adder_1_out), .en(clock_1_out), .clk(clock_1_out), .Q(rgb_video_1_p4), .clr(R));
  Register #(.width(7)) register_2 (.D(adder_2_out), .en(adder_1_cout), .clk(clock_1_out), .Q(rgb_video_1_p5), .clr(R));
  assign bit_extender_1_out = {{7{1'b0}}, 1'b1};  // Bit_Extender bit_extender_1
  assign bit_extender_2_out = {{6{1'b0}}, 1'b1};  // Bit_Extender bit_extender_2
  Adder adder_1 (.a(rgb_video_1_p4), .b(bit_extender_1_out), .out(adder_1_out), .cout(adder_1_cout));  // open: cin
  Adder #(.width(7)) adder_2 (.a(rgb_video_1_p5), .b(bit_extender_2_out), .out(adder_2_out));  // open: cin, cout
  ROM #(.addrWidth(15), .dataWidth(24)) rom_1 (.addr({rgb_video_1_p5, rgb_video_1_p4}), .data(rgb_video_1_p6));

  // Notes on the sheet:
  //   contents of rom_1 (hex, n*v repeats v):
  //   8cc4ff 8fc5ff 91c4fe 94c4fd 98c5fb 97c5fc 94c7fc 97c5f9 98c7f8 9cc8f9 9dc6f6 9ec7f9 9dc7fa 99cbfc
  //   8bc4f9 8bc4fd 8fc5fd 8dc3fe 82c0ff 76bcfe 7abdfd 88c1fd 95c8fe 95c8fb 96c9ff 98c8fe 92c4fd 83c0fa
  //   73bcfc 71bafa 76bbfc 78bcfc 82c3ff 7cbefd 72bdfe 73bdfe 72bbfe 6fb8fc 70b9fe 70b9fe 70b9fe 6fb8fc
  //   73bcff 74beff 73beff 76bcfc 76bdfd 75bcfc 77befe 76bdfe 7bbffd 8dc7ff 8ac7fa 8ec8fd 93c8fd 9acafc
  //   a1cbfd 9ccafc 9ccafb a7d1ff aed2fa b1d5f8 abd4f9 abd1fc aed3fc b1d4f8 b4d5f8 aad0f6 abd3fb b1d4f9
  //   b9d8fa bad9fc b8dafd b8d8f9 b8d9f9 badbfa b9d6f7 bbdafb b8dbfd aad0fe 8ec7f7 9cd1fd b6d7fc c1ddf7
  //   bedaf8 b7d7fc b0d6fe b2d7fd b8d9fb b8d9f9 b1d5fe b5d6fa bfdcfc c1ddf7 cce4f7 d7eaf7 daecf7 daeaf9
  //   d5e4fa c8e2fb abd3fb 92ccfa 91c8fa a1ccff 97c8f9 97ccf9 a6cffe 9fd0fd aad0fd b0d0fa b0d1f7 add0f5
  //   adcff3 accef1 a9cdf1 a9cef3 abcef3 a9cef1 a6c9f0 a6c8f0 a4c7ef a4c7ee a4c7ee a3c6ee a5caed a6caef
  //   a6caf0 a8ccf1 a8ceef acd0f0 afd3f1 b4d4f0 b4d2ee b6d5f1 b4d4f1 b0d2ee b5d5f0 bedaf3 c4dcf4 cce1f6
  //   cde4f7 c6dff4 c8e1f3 cee7f4 cbe4f2 c9dff4 c6ddf3 c4dcf2 c0d9f5 c0daf5 bddbf8 bbd9f9 b7dbfa a9d4fe
  //   9acafe 93c9fe 89c6fc 84c4fc 84c3fe 84c3fc 84c4fb 90cdfe 94cdfb 9acefc a4d4fd a9d4fc abd6ff abd5fe
  //   afd7fe add6ff acd5fe a8d3fd a7d3fd a8d5ff aad5fb add8fd acd8fe a4d3fb a1d2fc a0d2fe a2d1f9 a6d5fd
  //   a8d6fe a4d2fd a5d2fe a0d0fb 9ad0f9 9acffc 9cd1fe 9cd2fe 97ccfb 9cd0fc 9ad0fd 92cefc 8ecbfd 92ccfd
  //   96cbff 90cbfd 8dcafe 84c4fb 81c3fc 80c5ff 81c5fd 87c4fd 84c8fd 86c6fc 82c6fd 88c6fa b5dcfc a7d1f9
  //   aad9ff 9ecaf0 cde8ff d8e8fb dcedfa e2f0fb e8f2fb e9f3fc e5f2fb e3f1f8 e3f1f8 e6f4fc e2f0f9 e0eef7
  //   dfeff7 dfedf7 deeef9 dceefc cde5f6 cfe8fc c5e0fa b5dbff 99cbfb 95cefe 98cefd 9dd1fc add6fd c6e3fc
  //   d3e4f7 d9ebfc dbedfa e1f0fd e2eff8 e4f1f9 e4f1fa e4f1fa e5f1fa e2f2fb e0f1fa deeff9 dbedf8 d8eaf7
  //   dbeefa e0eefc eaffff 545053 87c2fd 8bc4fe 90c5fe 92c5fd 96c6fb 97c6fb 94c7fc 97c5f9 98c6f8 9cc8f9
  //   9dc6f6 9dc6f7 9dc7f6 9acafb 8ac4fe 7ebefb 7ebdfb 83c0fc 7dbffd 75bcfc 78bdfd 81c1fe 8cc6ff 88c4fe
  //   84c0fa 8ec3fd 92c9ff 7cbdfa 70bbfd 6fbbfe 6fb9fd 70b9fe 74bcff 71bafe 70bafb 70bafb 70b9fe 71bafe
  //   71baff 71baff 71baff 70b9fe 73bcff 73bdfe 72bdfe 75bbfb 75bcfc 74bbfb 77befe 76bdfe 78befb 8cc8fe
  //   92c9ff 8cc6fc 8ac5fd 94c9fe 9acbff 95cafb 9cccfc a6d0fe a8d0fd a8d2fc a4d0fc a4cefd a9cffd b1d3fb
  //   b5d6fb b2d4f9 b3d7fc b4d7fd b6d8fd b6d9fc b9dafc b9dbf8 b8dbf6 bbdaf7 bbd9fc b2d5ff a4d1fd 9ccffd
  //   9accfc a8d3fc b8d7f8 bcdaf8 b1d6fd a2d1fd 9dccfc a2d0fb acd3fa b0d4fb b5d9fa c1ddf7 d2e6fa d8e8f7
  //   e3effb eaf2fc e5f1fa e3f0f8 e1effa d2e9f6 bbdbfd aed2f9 aedaff 95cbfc 78befa 79bffc 94c8fe 93c7fb
  //   a0ccff a5cffe a7d1fd a8d0fd a8cffa a8d0f6 add1f4 afd1f2 aed0f2 acd0f3 a8ccf1 a8cbf1 a7caf0 a8cbf1
  //   a8cbf1 a8cbf1 a7cbf1 a9ccf2 abcdf2 adcff1 b2d3f1 b5d4f1 bad7f3 c2dcf3 c6def5 c3ddf4 c0dbf4 c6e0f9
  //   c4dcf5 c6ddf4 c9def4 cce1f5 cfe3f6 cde2f5 cae0f7 c8dff6 c4def2 c4def4 c4def3 c1dbf4 bed9f5 bbdaf6
  //   bad8f6 b8d8fb a7d3ff 87c4f8 78c3fd 7bc4fe 80c4ff 7fc4fe 7cc2fc 7bc3fd 7ec4fd 86c8fe 88c9fd 92cbff
  //   9bcffd a3d4fe a4d5fe a0d3fb a4d3f9 a8d4fb abd7fd addaff add9ff a9d5fb a8d5fc a8d5fc a6d3fb a7d6fe
  //   a6d5fd a3d3fb a5d5fd a2d1fb 9fd0fa a1d3fd a0d4ff 9bd0fc 94cefa 95ccfc 99cffc 9dd3fd 9cd0ff 9acefe
  //   95cefd 8fcbfc 90cdff 94cdfe 97ccfe 99cdfb 98cefd 90cbfb 8cc9fc 89c9fe 87c7ff 89c6ff 86cafe 89c8fe
  //   8cc4f4 cae6ff cbe7f7 c4e2f8 c5def9 d4ebff d4e9f7 d4e8f5 daedfb e3f2fe e8f5fe e5f2fc e0edf9 daebf7
  //   daebf8 ddedf7 e2f0fa e4f2fa e5f2fc e7f0fb e5f1fc e4f1fc ddecf7 dff0f9 dbedf9 c5e4fe a5d4fd a1d1fb
  //   aed9ff a3d3fb 97caf6 bde1fd d9edfc e3f1fd e6f4fb ecf6fe 4*e8f6ff e4f2fb e0eff9 dcecfa d8e8f7 d5e8f6
  //   d6e7f8 d4e7f6 d7edf6 dbeffa b6baca 85c2fa 8ac3fe 8fc7fe 91c5fc 94c7fb 95c7fc 95c7fc 96c5fa 99c7f9
  //   9cc8f9 9dc6f7 99cafc 98c9fd 97c8fe 8ec5fd 81bff9 82c2fc 79bcfa 79befd 75bcfb 76bdfb 77bbfa 7abbfb
  //   79bbfb 7ebffe 85c1fd 86c1fe 78bbfb 74bdfd 74bdfd 70b9fb 71b9fc 6fb8fd 70b9fe 71bcfc 71bcfc 71bafe
  //   72bbff 72bbfe 72bbfe 72bbfe 71bbfe 74bdff 74beff 73beff 76bcfc 76bdfd 75bcfc 77befe 76bdfe 75bcf9
  //   87c7fb 96c8ff 8ec6fe 85c7fe 8ac4fc 8dc4fc 96cbfe 98c9fa a3cdff a2cdff 9fceff 9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
endmodule

module Graphics_Card_128x64 (
  input  R
);

  wire adder_1_cout, clock_1_out;
  wire [5:0] adder_2_out, bit_extender_2_out, rgb_video_1_p5;
  wire [6:0] adder_1_out, bit_extender_1_out, rgb_video_1_p4;
  wire [23:0] rgb_video_1_p6;

  Clock clock_1 (.out(clock_1_out));
  // RGB_Video #(.cursor("No Cursor"), .height(64), .scale(4)) rgb_video_1: pin names not known; wires that end beside it: R, clock_1_out, clock_1_out, rgb_video_1_p4, rgb_video_1_p5, rgb_video_1_p6
  Register #(.width(7)) register_1 (.D(adder_1_out), .en(clock_1_out), .clk(clock_1_out), .Q(rgb_video_1_p4), .clr(R));
  Register #(.width(6)) register_2 (.D(adder_2_out), .en(adder_1_cout), .clk(clock_1_out), .Q(rgb_video_1_p5), .clr(R));
  assign bit_extender_1_out = {{6{1'b0}}, 1'b1};  // Bit_Extender bit_extender_1
  assign bit_extender_2_out = {{5{1'b0}}, 1'b1};  // Bit_Extender bit_extender_2
  Adder #(.width(7)) adder_1 (
    .a(rgb_video_1_p4), .b(bit_extender_1_out), .out(adder_1_out), .cout(adder_1_cout));  // open: cin
  Adder #(.width(6)) adder_2 (.a(rgb_video_1_p5), .b(bit_extender_2_out), .out(adder_2_out));  // open: cin, cout
  ROM #(.addrWidth(13), .dataWidth(24)) rom_1 (.addr({rgb_video_1_p5, rgb_video_1_p4}), .data(rgb_video_1_p6));

  // Notes on the sheet:
  //   contents of rom_1 (hex, n*v repeats v):
  //   15242b a191e 30f0f b09 20d09 40e0d 40f11 21013 51218 41316 31517 61818 a1c1e 112327 1b2936 20303f
  //   1d303e 1a303b 172933 f2027 d181c e181a 151f20 1c2627 202529 1d2729 152525 f2121 e1c1c 1d2323 221d21
  //   938d8d fefdf9 b6bbb4 919b93 d3ddd5 dde2dc 50524d 212620 131a13 5b655c cdd0c9 867878 ac9397 8a6a75
  //   dbc4cc fbf9fc f2fcfb f1fcfe f0feff e3efef e5f1f1 e9f3f4 eff9fa f1fbfc e9f3f4 f2fcfd f3fdfe f7ffff
  //   dbe6e8 cad8d9 ccdadb dfeef1 e6f5f8 e4f2f3 e0eeef ebf9fa f0feff e8f6f6 d1dfdf d5e3e3 c9d7d7 eefafa
  //   c3cfcf d4dfe1 f7ffff f5ffff e4eff1 eef7fc f7ffff feffff dddcda f0e6e7 fffcf9 fffef9 fefff8 fafff8
  //   fcfffb f7fdfb 899394 39484d 293c43 202e39 24323f 1f2c3d 1d2d3c 1a2d34 1f3238 19262e 1d2730 1e2b34
  //   16202a 171f2a 19212c 18212a 16232b 132529 132529 182327 1a2328 1b2628 1c2729 212b2d 232d2f 252d2f
  //   222a2c 232728 222627 212322 1e201f 1e1e1c 1b1b19 191917 171715 161815 161815 141613 131512 f1e23
  //   61518 c0c 907 10c08 40e0d 61113 51316 a171d 7161b 51719 81a1a f2123 16272e 1c2a37 1c2c3b 162836
  //   182a36 182933 15242b 121d21 121c1e 151f21 172122 21292c 182224 152022 152324 2d3939 192221 141615
  //   1e1e1c a1a39e adb2ab e2e4df d6d8d3 e8eae5 212620 2b322b 202a22 363b35 4c4b46 524444 d1bdbf bea9b0
  //   e1d5d9 f8f9fb f3fdfe effdfd eaf8f9 e7f5f5 d2dede e0ecec e7f1f2 e9f3f4 e4eeef e7f1f2 edf7f8 e8f3f5
  //   aeb9bb cad8d9 d3e1e2 e8f8f8 e5f5f5 e6f4f5 e8f4f4 f0fbfd f3ffff e8f4f4 eaf8f8 dbe7e7 e6f2f2 eefafa
  //   f7ffff f1fcfe eaf5f7 e1ecee edf8fa e1eaef eaf2f5 dce2e2 e9ebea dfdbda f8eaea d1b8bb fae5e4 fffcf8
  //   fdfffa fafffe f8ffff acbbbe 41545a 26343d 1e2c37 1a2a37 1e303a 1f3239 203339 222f37 202d35 1b2831
  //   202a34 1d2530 1b232e 1a242d 17262d 15272b 16252a 182327 1a2127 1a2426 1b2527 1c2628 1e282a 20282b
  //   1d2527 1e2326 1e2223 1d2122 1c1e1d 1d1f1e 1c1e1b 1a1a1a 171916 151716 121713 131514 111612 9181b
  //   21212 b08 a05 c08 5110f 81317 7141a 6131b 7161b 81a1c c1e20 152429 1a2930 1b2936 182535 14222f
  //   172530 19262f 17212a 121d21 111c1e 111b1d 101a1c 111b1d 161e21 21262a 181d20 111a19 1e2925 b1811
  //   5a675e effbf1 e7eae3 857b7a d3c7c7 c1c0be fbfffd c7d6cf a4afa7 52514d 342a29 554747 d1c7c6 fafcfb
  //   dbe4e1 f5ffff dceaea d5e3e3 ddedec daeae9 d7e5e5 cbdad7 dce8e6 e4f0ee e4f0ee e9f5f3 e6f2f0 effbfb
  //   d0dcdc c4d2d2 c5d3d3 ebfbfa e5f3f3 e7f3f3 f4fefd eaf4f5 f6ffff ebf5f4 e7f3f1 edf7f6 f5fffe f0faf9
  //   ecf6f5 ebf5f6 e0eaeb e5eff1 f0fafc d8e3e5 c9d4d6 e2eeee d9e3e2 edf2ee fae4e7 762b3f 772c40 e1c4c8
  //   faf9f5 f8fefa f7ffff e0f3f1 a9bdbe 233237 203236 162b30 152d31 1f3236 223438 24333a 202d35 233038
  //   27343c 26303a 232d37 1c2b32 1a2b32 192b2f 18272c 1b2228 1c2127 1d2027 1c2127 1a2328 1a2527 1a2426
  //   192124 161e21 181d20 161b1e 161a1b 121617 121615 141517 121615 121617 121816 141819 141a18 71717
  //   21211 e0b e09 4100c 81412 91418 61319 20f17 9181f f2125 112325 152429 16252c 15232e 12202d 14202e
  //   17232f 17212a 111c22 c171d d181c e191d f191b 151f21 182023 161b1f 23282b 131c19 2c3932 87988e d9ebdf
  //   f4fff6 ebede8 675f5d 877d7e e8e7e5 f1f7f3 e5f2eb f8fffd ada9a8 625857 cfc5c4 fcfbf9 d4dfdb d3e6e2
  //   dbeeec ccdfdd c3d3d2 ccdcdb d2e2e1 d8e8e7 d0dfdc d6e5e2 e3efed e5f1ef e1edeb e7f3f1 effbfb d4e0e0
  //   d6e4e4 cad8d8 dfefee e1f0ed f2fcfb f1faf9 e9efef ecf5f4 ecf5f4 f2fbfa f4fdfc eef8f7 f5fffe f3fdfc
  //   f1fbfc eef8f9 edf7f9 ebf5f7 c5d0d2 d3e1e2 b8c8c7 c6d5d2 f9ffff fff4fa b8667d 701b32 89646b eae2e0
  //   f0f2ef edefee b6b1b5 443d44 3c373d 1e1f23 324040 6b7d7d 5b6a6d 36454a 324148 25343b 28373e 25323a
  //   29333d 202d36 1f3037 1d2e35 1d2c33 1c292f 1e252d 1e2329 1d2228 1b2228 1b262a 1b262a 192428 162022
  //   131d1f 121a1d 11191c 111619 101518 f1515 101417 101616 111619 13181b 14191c 121a1c 31614 130f 1120c
  //   4130e a1614 c1818 a1519 51218 7141c e1d24 152429 16252a 142328 132229 121e2a f1b27 121c26 121f27
  //   101d25 a171d 91219 b141b c191f 101b1f 131a20 f171a 1b2527 535f5d b6c1bb d6e1d9 deeee1 cbd9cc f7fef7
  //   a0a5a1 ccd1cd b9bdbc eef2f1 ccd0cf dadedd eff1ee ececea a5a4a2 e8e7e5 f6f8f5 c6ccca ceddda cfe5e2
  //   b7d2cd bbcfcd bdd0ce cee1df d5e8e6 cededb cfdfdc ddece9 e2f1ee e5f1ef ecf8f6 f0fcfa d2dedc d7e6e3
  //   ccdbd8 d0dfdc dfebe9 f1faf9 f6fcfa e7ebea dee4e2 e9efed f2f8f6 f7fdfb f7fffd f5fe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
endmodule

module Graphics_Card_64x32 (
  input  R
);

  wire adder_1_cout, clock_1_out;
  wire [4:0] adder_2_out, bit_extender_2_out, rgb_video_1_p5;
  wire [5:0] adder_1_out, bit_extender_1_out, rgb_video_1_p4;
  wire [23:0] rgb_video_1_p6;

  Clock clock_1 (.out(clock_1_out));
  // RGB_Video #(.cursor("No Cursor"), .height(32), .scale(5), .width(64)) rgb_video_1: pin names not known; wires that end beside it: R, clock_1_out, clock_1_out, rgb_video_1_p4, rgb_video_1_p5, rgb_video_1_p6
  Register #(.width(6)) register_1 (.D(adder_1_out), .en(clock_1_out), .clk(clock_1_out), .Q(rgb_video_1_p4), .clr(R));
  Register #(.width(5)) register_2 (.D(adder_2_out), .en(adder_1_cout), .clk(clock_1_out), .Q(rgb_video_1_p5), .clr(R));
  assign bit_extender_1_out = {{5{1'b0}}, 1'b1};  // Bit_Extender bit_extender_1
  assign bit_extender_2_out = {{4{1'b0}}, 1'b1};  // Bit_Extender bit_extender_2
  Adder #(.width(6)) adder_1 (
    .a(rgb_video_1_p4), .b(bit_extender_1_out), .out(adder_1_out), .cout(adder_1_cout));  // open: cin
  Adder #(.width(5)) adder_2 (.a(rgb_video_1_p5), .b(bit_extender_2_out), .out(adder_2_out));  // open: cin, cout
  ROM #(.addrWidth(11), .dataWidth(24)) rom_1 (.addr({rgb_video_1_p5, rgb_video_1_p4}), .data(rgb_video_1_p6));

  // Notes on the sheet:
  //   contents of rom_1 (hex, n*v repeats v):
  //   828572 868975 898a76 8a8b77 888b77 878a77 858876 838575 7f8173 797d6f 72796b 6c7467 6a7168 697069
  //   6a706a 6b706a 676e68 666c66 696f69 737971 7d8076 878277 94826e af815c 9f7759 7a7160 596c6c 495957
  //   324037 2e3d36 2e3d35 2d3c36 2c3b36 2c3b38 2c3c39 2d3b3b 2b3a3b 293a3a 2a3a3b 2c3c3e 2c3d40 2f4043
  //   36454a 3e4c53 47535c 505962 575e66 5e656a 727574 89857e 959085 a09a8d a6a091 aca696 b4ae9f b8b2a6
  //   bfb8ae c5bcb6 cbc0bc d1c3c0 d4c6c3 d8c9c6 dacbc8 dbccc9 918f7a 91927c 94937e 93937d 91927d 8e917d
  //   8d907c 8a8d7a 858777 7f8173 7a7d6f 72796c 6e766b 6d746c 6d736c 6d736c 697169 616a63 5d6761 6d665b
  //   bd6644 ea6a21 f9790a f97c09 dc987b 81cfe7 61d8f6 76d9ec 609192 2e3e36 2d3b34 2b3b33 2b3a34 2c3a36
  //   2b3a37 2a3a37 293936 283837 263637 273738 29383b 293b3f 2c3d41 2f3f45 37464d 414d55 49555b 505a60
  //   63686c 787777 89867f 9b9489 a69f8e aba593 b2ac9d b9b3a6 c1bab0 c8bfb9 cec4c1 d3c6c4 d6c9c5 d9cbc7
  //   dacbc8 dbcbca 9f9d83 a09e85 a09f86 9f9d85 9b9b84 979883 949781 91947f 8d8e7c 878979 7f8373 777e6f
  //   747b6e 727a6f 70766f 6f746d 6a726b 636c64 8a6652 df6025 fb5f05 fa5b05 f64907 be688b 54c0ef 34c4f6
  //   41d0f8 64dbed 9cefce 9dbf76 5f6e3d 2b3932 2b3832 2a3833 293833 293736 283735 273734 253635 243635
  //   243636 26383a 27383e 27383e 2a3c42 32434a 3b4b50 445257 515c5f 62696b 777975 8c8a81 9c9889 a9a495
  //   b3ad9f b9b4a7 c2bab1 cac1bb cfc7c1 d2c8c6 d5cac8 d7cac7 d9cbc6 dacbc6 ada98e adaa8f adaa90 a8a58c
  //   a3a188 9f9f87 9b9d85 969882 919280 8b8d7c 858978 7d8373 797f71 757d71 737b71 70776e 6c736c 986f56
  //   f16715 f44d05 f33f05 e22b08 b22526 4ea0de 25b6f5 1caff1 41cfe4 75c966 9bd213 b3dd0e c9e12f a0b237
  //   455135 293832 283732 273633 263633 253532 253533 253534 233535 243638 24363c 24363b 26373e 2a3b42
  //   314347 38494f 415053 4f5a5c 656b69 7b7d78 96948a a8a597 b6b1a3 beb7ab c4bbb4 cbc2be d0c7c4 d3c9c7
  //   d5cbc9 d7ccc9 d8cbc5 d8cac2 b6b298 b5b196 b4af94 afac92 a8a68d a4a48a a1a187 9b9d85 959782 90927f
  //   8a8c7b 848778 7e8274 777f70 757e71 72796f 847165 eb591e e63a05 cd2907 c01d09 ad1c09 b13443 2e9fee
  //   16a1f1 1cbdf1 4fb08e 72b918 8fc105 9ebf05 b7ce06 c6d71c ced549 7a7f39 283730 273632 263633 253532
  //   243432 233432 223434 223436 243539 24363b 25363d 27383f 2b3d42 324348 37484c 425152 576263 737777
  //   91918a a8a59c b8b2aa c1bab3 c8c0bb cfc4c2 d2c9c8 d5ccca d5cbca d6cbc9 d5cac3 d5c9bf bdb79f bbb59a
  //   b9b498 b4b295 adac90 a9a78e a6a58b a2a188 9b9c85 959781 8f917e 898b7a 808577 798272 7e8579 b8bab2
  //   e9887b de2705 b82307 a7170c ae1206 b41808 862324 288bd8 12acf5 2cadd5 5fad4e 6da61a 85af0b 8caf04
  //   93ac07 a4b205 c0c606 cece16 8d9234 293831 253532 233431 223431 213432 213333 213436 223536 233638
  //   243739 24383b 273a3e 283c3f 2f4245 3a4b4e 505d61 6b7176 8b8c89 a8a59f bab3af c3bbb8 cac2bf d0c5c4
  //   d1c9c7 d3cbca d4cbcb d2cac7 d1c9bf cec6b8 c2bca4 c0bba1 bcb89b b7b597 b2b093 aead91 aba98e a5a58b
  //   a0a288 9a9c85 949782 8e917e 868b7b a5aa9f ebedea ebc8cc c32519 950d06 632d41 3d314d 652a39 a7190a
  //   901e1a 2a95dd 17a9f3 3ca5ab 5fa046 74a719 739f15 739514 88a00c 95aa09 9caf06 b3be05 c6ca2d a5a843
  //   2a3a31 233532 213431 203331 213333 1f3433 1f3435 203536 223738 233738 24373d 24393e 2b3f41 37484c
  //   4c5a60 666f75 888a8b a8a49f bab2b2 c3baba cac1bf cfc5c4 d1c8c6 d2cac8 d2cac7 cfc7c1 cbc5b8 c5bfaf
  //   c8c2aa c5bfa6 c1bca0 bcb89b b7b396 b4b094 b1ae91 aaa98e a5a48b a0a089 999b87 959787 c3c5bc f9faf8
  //   f4f3fa c38b9e 9b1105 81120e 39263b 9091a 473859 96190f 8a1923 339de8 23b9f2 42adab 61a549 659735
  //   658e2f 678327 81a00d 84a409 81980b 94a408 a5b30d b3bb2f 8c933d 243631 203331 203331 223232 203232
  //   1f3334 1f3435 203536 203537 22373c 23363c 283c40 36484d 4a595f 626b75 81868a a19f9e b6afb0 bfb7b7
  //   c7bfbf cdc4c5 d2c8c7 d4c9c8 d1c7c5 cac4ba c3bdad bab5a1 cbc5af c8c2aa c4bea5 c0bb9f bab69a b7b397
  //   b1af95 adab91 a9a78e a5a58d a3a28e d7d6cf faf4f6 f6e6ea e6c3c5 c48787 891e0b 7b160b 59364d 473657
  //   963453 a20905 a1120e 4891cb 24adeb 45afb2 5ea152 659731 608b25 577923 607f1f 698b15 779817 839b1c
  //   8da123 9bab27 b0b647 797f46 213331 203330 1f3131 1e3232 1e3334 1e3334 1f3435 1f3535 203638 223639
  //   263c3f 32474c 45565e 616a75 7a8188 939496 aba6a6 b7b1b1 c0baba c8c0c1 cec5c4 d2c8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
endmodule
